// Logisim project circuito.circ as structural Verilog: 1 circuit, main circuit main
module main (
  input  [7:0] Data,
  input  [7:0] Data_in,
  input  Clk,
  input  WrData_in,
  input  Rst,
  input  WrState,
  input  WrStateSize,
  input  WrTextSize,
  input  WrKeyStream,
  input  MK,
  input  Wr_J,
  input  Wr_I,
  input  Wr_K,
  input  Wr_temp,
  input  MS0,
  input  [1:0] MS1,
  input  [1:0] MS2,
  input  MADR,
  input  MOUT,
  output Status,
  output [7:0] address,
  output [7:0] Data_out
);

  wire rst_t;
  wire [7:0] adder_1_out, adder_2_out, divider_1_rem, multiplexer_1_out, multiplexer_2_out,
       multiplexer_3_out, multiplexer_4_out, multiplexer_5_out, RegData_in_q, RegI_q, RegJ_q, RegK_q,
       RegKeyStream_q, RegState_q, RegStateSize_q, RegTemp_q, RegTextSize_q;

  Register RegState (.D(Data), .en(WrState), .Q(RegState_q), .clk(Clk), .clr(rst_t));
  Register RegStateSize (.D(Data), .en(WrStateSize), .Q(RegStateSize_q), .clk(Clk), .clr(rst_t));
  Register RegTextSize (.D(Data), .en(WrTextSize), .Q(RegTextSize_q), .clk(Clk), .clr(rst_t));
  Register RegKeyStream (.D(Data), .en(WrKeyStream), .Q(RegKeyStream_q), .clk(Clk), .clr(rst_t));
  Register RegData_in (.en(WrData_in), .Q(RegData_in_q), .clk(Clk), .clr(rst_t));  // open: D
  Multiplexer #(.width(8), .enable("false")) multiplexer_1 (
    .in0(RegKeyStream_q), .in1(RegState_q), .out(multiplexer_1_out), .sel(MS0));
  Multiplexer #(.select(2), .width(8), .enable("false")) multiplexer_2 (
    .in0(RegTextSize_q), .in1(divider_1_rem), .in2(RegI_q), .in3(RegJ_q), .out(multiplexer_2_out), .sel(MS1));
  Register RegJ (.D(divider_1_rem), .en(Wr_J), .Q(RegJ_q), .clk(Clk), .clr(rst_t));
  Multiplexer #(.select(2), .width(8), .enable("false")) multiplexer_3 (
    .in0(RegI_q), .in1(RegJ_q), .in2(RegK_q), .in3(RegTemp_q), .out(multiplexer_3_out), .sel(MS2));
  Multiplexer #(.width(8), .enable("false")) multiplexer_4 (
    .in0(8'h1), .in1(RegData_in_q), .out(multiplexer_4_out), .sel(MS2[0]));
  Register RegI (.D(divider_1_rem), .en(Wr_I), .Q(RegI_q), .clk(Clk), .clr(rst_t));
  Multiplexer #(.width(8), .enable("false")) multiplexer_5 (
    .in0(Data), .in1(adder_2_out), .out(multiplexer_5_out), .sel(MK));
  Register RegK (.D(multiplexer_5_out), .en(Wr_K), .Q(RegK_q), .clk(Clk), .clr(rst_t));
  Adder adder_1 (.a(multiplexer_1_out), .b(multiplexer_2_out), .out(adder_1_out));  // open: cin, cout
  Adder adder_2 (.a(multiplexer_3_out), .b(multiplexer_4_out), .out(adder_2_out));  // open: cin, cout
  Comparator comparator_1 (.a(RegK_q), .b(adder_1_out), .lt(Status));  // open: gt, eq
  Divider divider_1 (.a(adder_2_out), .b(RegStateSize_q), .rem(divider_1_rem));  // open: out, upper
  Register RegTemp (.D(Data_in), .en(Wr_temp), .Q(RegTemp_q), .clk(Clk), .clr(rst_t));
  Multiplexer #(.width(8), .enable("false")) multiplexer_6 (.in0(adder_1_out), .in1(RegK_q), .out(address), .sel(MADR));
  Multiplexer #(.width(8), .enable("false")) multiplexer_7 (
    .in0(RegData_in_q), .in1(RegTemp_q), .out(Data_out), .sel(MOUT));
endmodule
