// Logisim project sincronizador.circ as structural Verilog: 1 circuit, main circuit main
module main (
  input  in,
  input  clk,
  output bt_out
);

  wire and_1_out, and_2_out, FF0_q, FF1_q, not_1_out, not_2_out, not_3_out, or_1_out, reset_out;

  Button reset (.out(reset_out));
  or or_1 (or_1_out, FF1_q, FF0_q);
  not not_1 (not_1_out, FF1_q);
  not not_2 (not_2_out, FF0_q);
  and and_1 (and_1_out, or_1_out, in);
  and and_2 (and_2_out, not_1_out, not_2_out, in);
  D_Flip_Flop FF1 (.clk(clk), .D(and_1_out), .Q(FF1_q), .reset(reset_out));  // open: Qn, preset, en
  D_Flip_Flop FF0 (.clk(clk), .D(and_2_out), .Q(FF0_q), .reset(reset_out));  // open: Qn, preset, en
  not not_3 (not_3_out, FF1_q);
  and and_3 (bt_out, not_3_out, FF0_q);
endmodule
