// Logisim project arc4-0704.circ as structural Verilog: 8 circuits, main circuit supraCircuito
module supraCircuito (
);

  controlPath controlpath_1 ();  // open: status, data_av
  dataPath datapath_1 ();  // open: Data, Data_in, Clk, Rst, WrState, WrStateSize, WrTextSize, WrKeyStream, WrData_in, MS1, MS0, Wr_J, Wr_I, MS2, MK, Wr_K, MADR, MOUT, Wr_temp, Status, address, Data_out
endmodule

module dataPath (
  input  [7:0] Data,
  input  [7:0] Data_in,
  input  Clk,
  input  WrData_in,
  input  Rst,
  input  WrState,
  input  WrStateSize,
  input  WrTextSize,
  input  WrKeyStream,
  input  MK,
  input  Wr_J,
  input  Wr_I,
  input  Wr_K,
  input  Wr_temp,
  input  MS0,
  input  [1:0] MS1,
  input  [1:0] MS2,
  input  MADR,
  input  MOUT,
  output Status,
  output [7:0] address,
  output [7:0] Data_out
);

  wire rst_t;
  wire [7:0] adder_1_out, adder_2_out, divider_1_rem, multiplexer_1_out, multiplexer_2_out,
       multiplexer_3_out, multiplexer_4_out, multiplexer_5_out, RegData_in_q, RegI_q, RegJ_q, RegK_q,
       RegKeyStream_q, RegState_q, RegStateSize_q, RegTemp_q, RegTextSize_q;

  Register RegState (.D(Data), .en(WrState), .Q(RegState_q), .clk(Clk), .clr(rst_t));
  Register RegStateSize (.D(Data), .en(WrStateSize), .Q(RegStateSize_q), .clk(Clk), .clr(rst_t));
  Register RegTextSize (.D(Data), .en(WrTextSize), .Q(RegTextSize_q), .clk(Clk), .clr(rst_t));
  Register RegKeyStream (.D(Data), .en(WrKeyStream), .Q(RegKeyStream_q), .clk(Clk), .clr(rst_t));
  Register RegData_in (.en(WrData_in), .Q(RegData_in_q), .clk(Clk), .clr(rst_t));  // open: D
  Multiplexer #(.width(8), .enable("false")) multiplexer_1 (
    .in0(RegKeyStream_q), .in1(RegState_q), .out(multiplexer_1_out), .sel(MS0));
  Multiplexer #(.select(2), .width(8), .enable("false")) multiplexer_2 (
    .in0(RegTextSize_q), .in1(divider_1_rem), .in2(RegI_q), .in3(RegJ_q), .out(multiplexer_2_out), .sel(MS1));
  Register RegJ (.D(divider_1_rem), .en(Wr_J), .Q(RegJ_q), .clk(Clk), .clr(rst_t));
  Multiplexer #(.select(2), .width(8), .enable("false")) multiplexer_3 (
    .in0(RegI_q), .in1(RegJ_q), .in2(RegK_q), .in3(RegTemp_q), .out(multiplexer_3_out), .sel(MS2));
  Multiplexer #(.width(8), .enable("false")) multiplexer_4 (
    .in0(8'h1), .in1(RegData_in_q), .out(multiplexer_4_out), .sel(MS2[0]));
  Register RegI (.D(divider_1_rem), .en(Wr_I), .Q(RegI_q), .clk(Clk), .clr(rst_t));
  Multiplexer #(.width(8), .enable("false")) multiplexer_5 (
    .in0(Data), .in1(adder_2_out), .out(multiplexer_5_out), .sel(MK));
  Register RegK (.D(multiplexer_5_out), .en(Wr_K), .Q(RegK_q), .clk(Clk), .clr(rst_t));
  Adder adder_1 (.a(multiplexer_1_out), .b(multiplexer_2_out), .out(adder_1_out));  // open: cin, cout
  Adder adder_2 (.a(multiplexer_3_out), .b(multiplexer_4_out), .out(adder_2_out));  // open: cin, cout
  Comparator comparator_1 (.a(RegK_q), .b(adder_1_out), .lt(Status));  // open: gt, eq
  Divider divider_1 (.a(adder_2_out), .b(RegStateSize_q), .rem(divider_1_rem));  // open: out, upper
  Register RegTemp (.D(Data_in), .en(Wr_temp), .Q(RegTemp_q), .clk(Clk), .clr(rst_t));
  Multiplexer #(.width(8), .enable("false")) multiplexer_6 (.in0(adder_1_out), .in1(RegK_q), .out(address), .sel(MADR));
  Multiplexer #(.width(8), .enable("false")) multiplexer_7 (
    .in0(RegData_in_q), .in1(RegTemp_q), .out(Data_out), .sel(MOUT));
endmodule

module controlPath (
  input  status,
  input  data_av
);

  wire clock_1_out, nextstate_1_d0, nextstate_1_d1, nextstate_1_d2, nextstate_1_d3, Q0_q, Q1_q, Q2_q, Q3_q;

  nextState nextstate_1 (
    .Status(status), .data_av(data_av), .D3(nextstate_1_d3), .Q3(Q3_q), .Q2(Q2_q), .Q1(Q1_q), .Q0(Q0_q),
    .D2(nextstate_1_d2), .D1(nextstate_1_d1), .D0(nextstate_1_d0));
  Clock clock_1 (.out(clock_1_out));
  D_Flip_Flop Q3 (.clk(clock_1_out), .D(nextstate_1_d3), .Q(Q3_q));  // open: Qn, preset, en, reset
  D_Flip_Flop Q2 (.clk(clock_1_out), .D(nextstate_1_d2), .Q(Q2_q));  // open: Qn, preset, en, reset
  D_Flip_Flop Q1 (.clk(clock_1_out), .D(nextstate_1_d1), .Q(Q1_q));  // open: Qn, preset, en, reset
  D_Flip_Flop Q0 (.clk(clock_1_out), .D(nextstate_1_d0), .Q(Q0_q));  // open: Qn, preset, en, reset
  outWrites outwrites_1 ();  // open: data_av, Q3, Q2, Q1, Q0, WrState, WrStateSize, WrTextSize, WrKeyStream, WrDataIn, Wr_J, Wr_I, Wr_K, WrTemp
  outMux outmux_1 ();  // open: Q3, Q2, Q1, Q0, MOUT, MADRK, MS2, MS1, MS0
  outGeral outgeral_1 ();  // open: status, Q3, Q2, Q1, Q0, data_av, Id, Sel, Done, Rst
endmodule

module nextState (
  input  Status,
  input  data_av,
  input  Q3,
  input  Q2,
  input  Q1,
  input  Q0,
  output D3,
  output D2,
  output D1,
  output D0
);

  wire and_1_out, and_2_out, and_3_out, and_4_out, and_5_out, and_6_out, and_7_out, and_8_out, and_9_out,
       and_10_out, and_11_out, and_12_out, and_13_out, and_14_out, and_15_out, and_16_out, and_17_out,
       and_18_out, and_19_out, not_1_out, not_2_out, not_3_out, not_4_out, not_5_out, not_6_out, not_7_out,
       not_8_out, not_9_out, not_10_out, not_11_out, not_12_out, not_13_out, not_14_out, not_15_out,
       not_16_out, not_17_out, not_18_out, not_19_out, not_20_out, not_21_out, not_22_out, not_23_out,
       not_24_out, not_25_out, not_26_out, not_27_out, not_28_out, not_29_out, not_30_out, not_31_out,
       not_32_out, not_33_out, not_34_out, not_35_out, not_36_out;

  not not_1 (not_1_out, Q3);
  not not_2 (not_2_out, Q2);
  not not_3 (not_3_out, Q3);
  not not_4 (not_4_out, Q1);
  not not_5 (not_5_out, Q3);
  not not_6 (not_6_out, Q0);
  not not_7 (not_7_out, Q2);
  not not_8 (not_8_out, Q1);
  not not_9 (not_9_out, Q0);
  not not_10 (not_10_out, Q2);
  not not_11 (not_11_out, Q3);
  not not_12 (not_12_out, Q1);
  not not_13 (not_13_out, data_av);
  not not_14 (not_14_out, Q3);
  not not_15 (not_15_out, Q2);
  not not_16 (not_16_out, Q3);
  not not_17 (not_17_out, Q0);
  not not_18 (not_18_out, Q2);
  not not_19 (not_19_out, Q0);
  not not_20 (not_20_out, Q3);
  not not_21 (not_21_out, Q1);
  not not_22 (not_22_out, Q2);
  not not_23 (not_23_out, Q1);
  not not_24 (not_24_out, Q3);
  not not_25 (not_25_out, Q1);
  not not_26 (not_26_out, data_av);
  not not_27 (not_27_out, Q3);
  not not_28 (not_28_out, Q2);
  not not_29 (not_29_out, Q3);
  not not_30 (not_30_out, Q0);
  not not_31 (not_31_out, Q2);
  not not_32 (not_32_out, Q0);
  not not_33 (not_33_out, Q2);
  not not_34 (not_34_out, Q0);
  not not_35 (not_35_out, Q3);
  not not_36 (not_36_out, Q0);
  and and_1 (and_1_out, not_1_out, Q2, Q1, Q0);
  and and_2 (and_2_out, Q3, not_2_out);
  and and_3 (and_3_out, not_3_out, Q2, not_4_out, Q0);
  and and_4 (and_4_out, not_5_out, Q2, Q1, not_6_out);
  and and_5 (and_5_out, Q3, not_7_out, Q1, Q0);
  and and_6 (and_6_out, Q3, Q2, not_8_out, not_9_out);
  and and_7 (and_7_out, data_av, not_10_out, Q1, Q0);
  and and_8 (and_8_out, Status, not_11_out, Q2, not_12_out);
  and and_9 (and_9_out, not_13_out, not_14_out, not_15_out, Q1);
  and and_10 (and_10_out, not_16_out, Q1, not_17_out);
  and and_11 (and_11_out, not_18_out, Q1, not_19_out);
  and and_12 (and_12_out, not_20_out, Q2, not_21_out, Q0);
  and and_13 (and_13_out, Q3, not_22_out, not_23_out, Q0);
  and and_14 (and_14_out, data_av, not_24_out, not_25_out, Q0);
  and and_15 (and_15_out, not_26_out, not_27_out, not_28_out, Q0);
  and and_16 (and_16_out, not_29_out, Q2, Q1, not_30_out);
  and and_17 (and_17_out, Q3, not_31_out, not_32_out);
  and and_18 (and_18_out, data_av, not_33_out, not_34_out);
  and and_19 (and_19_out, Status, not_35_out, Q2, not_36_out);
  or or_1 (D3, and_1_out, and_2_out);
  or or_2 (D2, and_3_out, and_4_out, and_5_out, and_6_out, and_7_out, and_8_out);
  or or_3 (D1, and_9_out, and_10_out, and_11_out, and_12_out, and_13_out, and_14_out);
  or or_4 (D0, and_15_out, and_16_out, and_17_out, and_18_out, and_19_out);

  // Notes on the sheet:
  //   FUNCIONAMENTO TA VERIFICADO
  //   SE TIVER PROBLEMA AQ N Ë
endmodule

module outputCrtlPath (
  input  [7:0] Data,
  input  data_av,
  input  Q3,
  input  Q2,
  input  Q1,
  input  Q0
);
endmodule

module outWrites (
  input  data_av,
  input  Q3,
  input  Q2,
  input  Q1,
  input  Q0,
  output WrState,
  output WrStateSize,
  output WrTextSize,
  output WrKeyStream,
  output WrDataIn,
  output Wr_J,
  output Wr_I,
  output Wr_K,
  output WrTemp
);

  wire and_1_out, and_2_out, and_3_out, and_4_out, and_11_out, and_12_out, not_1_out, not_2_out, not_3_out,
       not_4_out, not_5_out, not_6_out, not_7_out, not_8_out, not_9_out, not_10_out, not_11_out, not_12_out,
       not_13_out, not_14_out, not_15_out, not_16_out, not_17_out, not_18_out, not_19_out, not_20_out,
       not_21_out, not_22_out, not_23_out, not_24_out, not_25_out, not_26_out, not_27_out, not_28_out,
       not_29_out, not_30_out;

  not not_1 (not_1_out, data_av);
  not not_2 (not_2_out, Q2);
  not not_3 (not_3_out, Q1);
  not not_4 (not_4_out, Q0);
  not not_5 (not_5_out, Q3);
  not not_6 (not_6_out, Q2);
  not not_7 (not_7_out, Q1);
  not not_8 (not_8_out, Q0);
  not not_9 (not_9_out, Q3);
  not not_10 (not_10_out, Q2);
  not not_11 (not_11_out, Q1);
  not not_12 (not_12_out, Q2);
  not not_13 (not_13_out, Q1);
  not not_14 (not_14_out, Q0);
  not not_15 (not_15_out, Q3);
  not not_16 (not_16_out, Q2);
  not not_17 (not_17_out, Q0);
  not not_18 (not_18_out, Q3);
  not not_19 (not_19_out, Q2);
  not not_20 (not_20_out, Q3);
  not not_21 (not_21_out, Q0);
  not not_22 (not_22_out, Q3);
  not not_23 (not_23_out, Q3);
  not not_24 (not_24_out, Q1);
  not not_25 (not_25_out, Q3);
  not not_26 (not_26_out, Q2);
  not not_27 (not_27_out, Q2);
  not not_28 (not_28_out, Q1);
  not not_29 (not_29_out, Q0);
  not not_30 (not_30_out, Q2);
  and and_1 (and_1_out, not_1_out, Q3, not_2_out, not_3_out, not_4_out);
  and and_2 (and_2_out, data_av, not_5_out, not_6_out, not_7_out, not_8_out);
  and and_3 (and_3_out, data_av, not_9_out, not_10_out, not_11_out, Q0);
  and and_4 (and_4_out, data_av, Q3, not_12_out, not_13_out, not_14_out);
  and and_5 (WrTextSize, data_av, not_15_out, not_16_out, Q1, not_17_out);
  and and_6 (WrKeyStream, data_av, not_18_out, not_19_out, Q1, Q0);
  and and_7 (WrDataIn, not_20_out, Q2, Q1, not_21_out);
  and and_8 (Wr_J, not_22_out, Q2, Q1, Q0);
  and and_9 (Wr_I, not_23_out, Q2, not_24_out, Q0);
  and and_10 (Wr_K, data_av, not_25_out, not_26_out, Q1, Q0);
  and and_11 (and_11_out, Q3, not_27_out, not_28_out, not_29_out);
  and and_12 (and_12_out, Q3, not_30_out, Q1, Q0);
  or or_1 (WrState, and_1_out, and_2_out);
  or or_2 (WrStateSize, and_3_out, and_4_out);
  or or_3 (WrTemp, and_11_out, and_12_out);
endmodule

module outMux (
  input  Q3,
  input  Q2,
  input  Q1,
  input  Q0,
  output MOUT,
  output MADRK,
  output [1:0] MS2,
  output [1:0] MS1,
  output MS0
);

  wire and_1_out, and_2_out, and_5_out, and_6_out, and_7_out, and_8_out, and_9_out, and_11_out, and_12_out,
       not_1_out, not_2_out, not_3_out, not_4_out, not_5_out, not_6_out, not_7_out, not_8_out, not_9_out,
       not_10_out, not_11_out, not_12_out, not_13_out, not_14_out, not_15_out, not_16_out, not_17_out;

  not not_1 (not_1_out, Q2);
  and and_1 (and_1_out, not_1_out, not_2_out, Q0);
  not not_2 (not_2_out, Q1);
  and and_2 (and_2_out, Q3, Q2);
  and and_3 (MADRK, Q3, Q2);
  not not_3 (not_3_out, Q2);
  not not_4 (not_4_out, Q0);
  not not_5 (not_5_out, Q3);
  not not_6 (not_6_out, Q2);
  not not_7 (not_7_out, Q0);
  and and_4 (MS1[1], Q3, not_8_out, not_9_out);
  not not_8 (not_8_out, Q2);
  not not_9 (not_9_out, Q1);
  not not_10 (not_10_out, Q3);
  and and_5 (and_5_out, not_10_out, Q2, Q0);
  not not_11 (not_11_out, Q2);
  and and_6 (and_6_out, Q3, not_11_out, not_12_out);
  not not_12 (not_12_out, Q0);
  not not_13 (not_13_out, Q3);
  and and_7 (and_7_out, not_13_out, Q2, Q0);
  not not_14 (not_14_out, Q2);
  and and_8 (and_8_out, Q3, not_14_out, not_15_out);
  not not_15 (not_15_out, Q1);
  and and_9 (and_9_out, Q3, not_16_out, not_17_out);
  not not_16 (not_16_out, Q2);
  not not_17 (not_17_out, Q0);
  or or_1 (MOUT, and_1_out, and_2_out);
  and and_10 (MS2[1], Q3, not_3_out, Q1, not_4_out);
  and and_11 (and_11_out, not_5_out, Q2, Q1, Q0);
  or or_2 (MS2[0], and_11_out, and_12_out);
  and and_12 (and_12_out, Q3, not_6_out, Q1, not_7_out);
  or or_3 (MS1[0], and_5_out, and_6_out);
  or or_4 (MS0, and_7_out, and_8_out, and_9_out);
endmodule

module outGeral (
  input  status,
  input  Q3,
  input  Q2,
  input  Q1,
  input  Q0,
  input  data_av,
  output Id,
  output Sel,
  output Done,
  output Rst
);

  wire and_1_out, and_2_out, and_3_out, and_4_out, and_5_out, not_1_out, not_2_out, not_3_out, not_4_out,
       not_5_out, not_6_out, not_7_out;

  not not_1 (not_1_out, Q0);
  not not_2 (not_2_out, Q1);
  not not_3 (not_3_out, Q0);
  not not_4 (not_4_out, status);
  not not_5 (not_5_out, Q3);
  not not_6 (not_6_out, Q1);
  not not_7 (not_7_out, Q0);
  and and_1 (and_1_out, Q2, Q0);
  and and_2 (and_2_out, Q3, Q1, not_1_out);
  and and_3 (and_3_out, Q2, Q0);
  and and_4 (and_4_out, Q3, not_2_out);
  and and_5 (and_5_out, Q3, not_3_out);
  and and_6 (Done, not_4_out, not_5_out, Q2, not_6_out, not_7_out);
  and and_7 (Rst, ~data_av, ~Q3, ~Q2, ~Q1, ~Q0);  // AND_Gate
  or or_1 (Id, and_1_out, and_2_out);
  or or_2 (Sel, and_3_out, and_4_out, and_5_out);
endmodule
