// Logisim project arc4-main.circ as structural Verilog: 8 circuits, main circuit controlPath
module supraCircuito (
  input  data_av,
  input  [7:0] data,
  output status,
  output Done,
  output [3:0] Estado
);

  wire button_1_out, clk, controlpath_1_id, controlpath_1_madrk, controlpath_1_mcomp, controlpath_1_mout,
       controlpath_1_ms0, controlpath_1_reset, controlpath_1_sel, controlpath_1_wr_i, controlpath_1_wr_j,
       controlpath_1_wr_k, controlpath_1_wrdatain, controlpath_1_wrkeystream, controlpath_1_wrstate,
       controlpath_1_wrstatesize, controlpath_1_wrtemp, controlpath_1_wrtextsize, not_1_out, or_1_out,
       sincronizador_1_bt_out;
  wire [1:0] controlpath_1_ms1, controlpath_1_ms2;
  wire [7:0] datapath_1_address, datapath_1_data_out, ram_1_data, register_1_q;

  Clock clock_1 (.out(clk));
  controlPath controlpath_1 (
    .status(status), .data_av(sincronizador_1_bt_out), .clk(clk), .WrState(controlpath_1_wrstate),
    .WrStateSize(controlpath_1_wrstatesize), .WrTextSize(controlpath_1_wrtextsize),
    .WrKeyStream(controlpath_1_wrkeystream), .WrDataIn(controlpath_1_wrdatain), .Wr_J(controlpath_1_wr_j),
    .Wr_I(controlpath_1_wr_i), .Wr_K(controlpath_1_wr_k), .WrTemp(controlpath_1_wrtemp),
    .MOUT(controlpath_1_mout), .MADRK(controlpath_1_madrk), .MS2(controlpath_1_ms2), .MS1(controlpath_1_ms1),
    .MS0(controlpath_1_ms0), .Id(controlpath_1_id), .Sel(controlpath_1_sel), .Done(Done),
    .Reset(controlpath_1_reset), .Rst(button_1_out), .Estado(Estado), .MCOMP(controlpath_1_mcomp));
  sincronizador sincronizador_1 (.in(data_av), .clk(clk), .bt_out(sincronizador_1_bt_out));
  Button button_1 (.out(button_1_out));
  RAM ram_1 (
    .addr(datapath_1_address), .data(ram_1_data), .sel(controlpath_1_sel), .clk(clk), .ld(controlpath_1_id));  // open: clr
  assign ram_1_data = not_1_out ? datapath_1_data_out : 8'bz;  // Controlled_Buffer controlled_buffer_1
  not not_1 (not_1_out, controlpath_1_id);
  dataPath datapath_1 (
    .Data(data), .Data_in(register_1_q), .Clk(clk), .Rst(or_1_out), .Status(status),
    .address(datapath_1_address), .Data_out(datapath_1_data_out), .WrState(controlpath_1_wrstate),
    .WrStateSize(controlpath_1_wrstatesize), .WrTextSize(controlpath_1_wrtextsize),
    .WrKeyStream(controlpath_1_wrkeystream), .WrData_in(controlpath_1_wrdatain), .MS1(controlpath_1_ms1),
    .MS0(controlpath_1_ms0), .Wr_J(controlpath_1_wr_j), .Wr_I(controlpath_1_wr_i), .MS2(controlpath_1_ms2),
    .MK(controlpath_1_madrk), .Wr_K(controlpath_1_wr_k), .MOUT(controlpath_1_mout),
    .Wr_temp(controlpath_1_wrtemp), .MCOMP(controlpath_1_mcomp));  // open: out_20
  or or_1 (or_1_out, controlpath_1_reset, button_1_out);
  Register register_1 (.D(ram_1_data), .en(controlpath_1_sel), .Q(register_1_q), .clk(clk));  // open: clr

  // Notes on the sheet:
  //   refatorar mk e madr dentro do datapath
endmodule

module controlPath (
  input  status,
  input  data_av,
  input  Rst,
  input  clk,
  output WrState,
  output WrStateSize,
  output WrTextSize,
  output WrKeyStream,
  output WrDataIn,
  output Wr_J,
  output Wr_I,
  output Wr_K,
  output WrTemp,
  output MOUT,
  output MADRK,
  output [1:0] MS2,
  output [1:0] MS1,
  output MS0,
  output MCOMP,
  output Id,
  output Sel,
  output Done,
  output Reset,
  output [3:0] Estado
);

  wire nextstate_1_d0, nextstate_1_d1, nextstate_1_d2, nextstate_1_d3;

  nextState nextstate_1 (
    .Status(status), .data_av(data_av), .D3(nextstate_1_d3), .Q3(Estado[3]), .Q2(Estado[2]), .Q1(Estado[1]),
    .Q0(Estado[0]), .D2(nextstate_1_d2), .D1(nextstate_1_d1), .D0(nextstate_1_d0));
  D_Flip_Flop Q3 (.clk(clk), .D(nextstate_1_d3), .Q(Estado[3]), .reset(Rst));  // open: Qn, preset, en
  D_Flip_Flop Q2 (.clk(clk), .D(nextstate_1_d2), .Q(Estado[2]), .reset(Rst));  // open: Qn, preset, en
  D_Flip_Flop Q1 (.clk(clk), .D(nextstate_1_d1), .Q(Estado[1]), .reset(Rst));  // open: Qn, preset, en
  D_Flip_Flop Q0 (.clk(clk), .D(nextstate_1_d0), .Q(Estado[0]), .reset(Rst));  // open: Qn, preset, en
  outWrites outwrites_1 (
    .data_av(data_av), .Q3(Estado[3]), .Q2(Estado[2]), .Q1(Estado[1]), .Q0(Estado[0]), .WrState(WrState),
    .WrStateSize(WrStateSize), .WrTextSize(WrTextSize), .WrKeyStream(WrKeyStream), .WrDataIn(WrDataIn),
    .Wr_J(Wr_J), .Wr_I(Wr_I), .Wr_K(Wr_K), .WrTemp(WrTemp));
  outMux outmux_1 (
    .Q3(Estado[3]), .Q2(Estado[2]), .Q1(Estado[1]), .Q0(Estado[0]), .MOUT(MOUT), .MADRK(MADRK), .MS2(MS2),
    .MS1(MS1), .MS0(MS0), .MCOMP(MCOMP));
  outGeral outgeral_1 (
    .status(status), .Q3(Estado[3]), .Q2(Estado[2]), .Q1(Estado[1]), .Q0(Estado[0]), .data_av(data_av),
    .Id(Id), .Sel(Sel), .Done(Done), .Rst(Reset));
endmodule

module dataPath (
  input  [7:0] Data,
  input  [7:0] Data_in,
  input  Clk,
  input  WrData_in,
  input  Rst,
  input  WrState,
  input  WrStateSize,
  input  WrTextSize,
  input  WrKeyStream,
  input  MK,
  input  Wr_J,
  input  Wr_I,
  input  Wr_K,
  input  Wr_temp,
  input  MS0,
  input  [1:0] MS1,
  input  MCOMP,
  input  [1:0] MS2,
  input  MOUT,
  output [7:0] out_20,
  output Status,
  output [7:0] address,
  output [7:0] Data_out
);

  wire nand_1_out, or_2_out, rst_t;
  wire [7:0] adder_1_out, adder_2_out, divider_1_out, divider_1_rem, multiplexer_1_out, multiplexer_2_out,
       multiplexer_3_out, multiplexer_5_out, multiplexer_6_out, multiplexer_7_out, RegData_in_q, RegI_q,
       RegJ_q, RegK_q, RegKeyStream_q, RegState_q, RegStateSize_q, RegTemp_q, RegTextSize_q;

  Register RegState (.D(Data), .en(WrState), .Q(RegState_q), .clk(Clk), .clr(rst_t));
  Register RegStateSize (.D(Data), .en(WrStateSize), .Q(RegStateSize_q), .clk(Clk), .clr(rst_t));
  Register RegTextSize (.D(Data), .en(WrTextSize), .Q(RegTextSize_q), .clk(Clk), .clr(rst_t));
  Register RegKeyStream (.D(Data), .en(WrKeyStream), .Q(RegKeyStream_q), .clk(Clk), .clr(rst_t));
  Register RegData_in (.D(Data_in), .en(WrData_in), .Q(RegData_in_q), .clk(Clk), .clr(rst_t));
  Multiplexer #(.width(8), .enable("false")) multiplexer_1 (
    .in0(RegKeyStream_q), .in1(RegState_q), .out(multiplexer_1_out), .sel(MS0));
  Multiplexer #(.select(2), .width(8), .enable("false")) multiplexer_2 (
    .in0(RegTextSize_q), .in1(divider_1_rem), .in2(RegI_q), .in3(RegJ_q), .out(multiplexer_2_out), .sel(MS1));
  Register RegJ (.D(divider_1_rem), .en(Wr_J), .Q(RegJ_q), .clk(Clk), .clr(rst_t));
  Multiplexer #(.select(2), .width(8), .enable("false")) multiplexer_3 (
    .in0(RegI_q), .in1(RegJ_q), .in2(RegK_q), .in3(RegTemp_q), .out(multiplexer_3_out), .sel(MS2));
  Multiplexer #(.width(8), .enable("false")) multiplexer_4 (.in0(8'h1), .in1(RegData_in_q), .out(out_20), .sel(MS2[0]));
  Register RegI (.D(divider_1_rem), .en(Wr_I), .Q(RegI_q), .clk(Clk), .clr(rst_t));
  Multiplexer #(.width(8), .enable("false")) multiplexer_5 (
    .in0(Data), .in1(adder_2_out), .out(multiplexer_5_out), .sel(MK));
  Register RegK (.D(multiplexer_5_out), .en(Wr_K), .Q(RegK_q), .clk(Clk), .clr(rst_t));
  Adder adder_1 (.a(multiplexer_1_out), .b(multiplexer_2_out), .out(adder_1_out));  // open: cin, cout
  Adder adder_2 (.a(multiplexer_3_out), .b(out_20), .out(adder_2_out));  // open: cin, cout
  Multiplexer #(.width(8), .enable("false")) multiplexer_6 (
    .in0(adder_2_out), .in1(RegK_q), .out(multiplexer_6_out), .sel(MCOMP));
  Multiplexer #(.width(8), .enable("false")) multiplexer_7 (
    .in0(RegStateSize_q), .in1(RegTextSize_q), .out(multiplexer_7_out), .sel(MCOMP));
  Register RegTemp (.D(Data_in), .en(Wr_temp), .Q(RegTemp_q), .clk(Clk), .clr(rst_t));
  Divider divider_1 (
    .a(multiplexer_6_out), .b(multiplexer_7_out), .out(divider_1_out), .rem(divider_1_rem));  // open: upper
  Multiplexer #(.width(8), .enable("false")) multiplexer_8 (.in0(adder_1_out), .in1(RegK_q), .out(address), .sel(MK));
  Multiplexer #(.width(8), .enable("false")) multiplexer_9 (
    .in0(RegData_in_q), .in1(RegTemp_q), .out(Data_out), .sel(MOUT));
  nand nand_1 (nand_1_out, divider_1_out[0], ~divider_1_out[1], ~divider_1_out[2], ~divider_1_out[3], ~divider_1_out[4], ~divider_1_out[5], ~divider_1_out[6], ~divider_1_out[7]);  // NAND_Gate
  or or_1 (Status, nand_1_out, or_2_out);
  or or_2 (or_2_out, divider_1_rem[0], divider_1_rem[1], divider_1_rem[2], divider_1_rem[3], divider_1_rem[4], divider_1_rem[5], divider_1_rem[6], divider_1_rem[7]);
endmodule

module nextState (
  input  Status,
  input  data_av,
  input  Q3,
  input  Q2,
  input  Q1,
  input  Q0,
  output D3,
  output D2,
  output D1,
  output D0
);

  wire and_1_out, and_2_out, and_3_out, and_4_out, and_5_out, and_6_out, and_7_out, and_8_out, and_9_out,
       and_10_out, and_11_out, and_12_out, and_13_out, and_14_out, and_15_out, and_16_out, and_17_out,
       and_18_out, and_19_out, not_1_out, not_2_out, not_3_out, not_4_out, not_5_out, not_6_out, not_7_out,
       not_8_out, not_9_out, not_10_out, not_11_out, not_12_out, not_13_out, not_14_out, not_15_out,
       not_16_out, not_17_out, not_18_out, not_19_out, not_20_out, not_21_out, not_22_out, not_23_out,
       not_24_out, not_25_out, not_26_out, not_27_out, not_28_out, not_29_out, not_30_out, not_31_out,
       not_32_out, not_33_out, not_34_out, not_35_out, not_36_out;

  not not_1 (not_1_out, Q3);
  not not_2 (not_2_out, Q2);
  not not_3 (not_3_out, Q3);
  not not_4 (not_4_out, Q1);
  not not_5 (not_5_out, Q3);
  not not_6 (not_6_out, Q0);
  not not_7 (not_7_out, Q2);
  not not_8 (not_8_out, Q1);
  not not_9 (not_9_out, Q0);
  not not_10 (not_10_out, Q2);
  not not_11 (not_11_out, Q3);
  not not_12 (not_12_out, Q1);
  not not_13 (not_13_out, data_av);
  not not_14 (not_14_out, Q3);
  not not_15 (not_15_out, Q2);
  not not_16 (not_16_out, Q3);
  not not_17 (not_17_out, Q0);
  not not_18 (not_18_out, Q2);
  not not_19 (not_19_out, Q0);
  not not_20 (not_20_out, Q3);
  not not_21 (not_21_out, Q1);
  not not_22 (not_22_out, Q2);
  not not_23 (not_23_out, Q1);
  not not_24 (not_24_out, Q3);
  not not_25 (not_25_out, Q1);
  not not_26 (not_26_out, data_av);
  not not_27 (not_27_out, Q3);
  not not_28 (not_28_out, Q2);
  not not_29 (not_29_out, Q3);
  not not_30 (not_30_out, Q0);
  not not_31 (not_31_out, Q2);
  not not_32 (not_32_out, Q0);
  not not_33 (not_33_out, Q2);
  not not_34 (not_34_out, Q0);
  not not_35 (not_35_out, Q3);
  not not_36 (not_36_out, Q0);
  and and_1 (and_1_out, not_1_out, Q2, Q1, Q0);
  and and_2 (and_2_out, Q3, not_2_out);
  and and_3 (and_3_out, not_3_out, Q2, not_4_out, Q0);
  and and_4 (and_4_out, not_5_out, Q2, Q1, not_6_out);
  and and_5 (and_5_out, Q3, not_7_out, Q1, Q0);
  and and_6 (and_6_out, Q3, Q2, not_8_out, not_9_out);
  and and_7 (and_7_out, data_av, not_10_out, Q1, Q0);
  and and_8 (and_8_out, Status, not_11_out, Q2, not_12_out);
  and and_9 (and_9_out, not_13_out, not_14_out, not_15_out, Q1);
  and and_10 (and_10_out, not_16_out, Q1, not_17_out);
  and and_11 (and_11_out, not_18_out, Q1, not_19_out);
  and and_12 (and_12_out, not_20_out, Q2, not_21_out, Q0);
  and and_13 (and_13_out, Q3, not_22_out, not_23_out, Q0);
  and and_14 (and_14_out, data_av, not_24_out, not_25_out, Q0);
  and and_15 (and_15_out, not_26_out, not_27_out, not_28_out, Q0);
  and and_16 (and_16_out, not_29_out, Q2, Q1, not_30_out);
  and and_17 (and_17_out, Q3, not_31_out, not_32_out);
  and and_18 (and_18_out, data_av, not_33_out, not_34_out);
  and and_19 (and_19_out, Status, not_35_out, Q2, not_36_out);
  or or_1 (D3, and_1_out, and_2_out);
  or or_2 (D2, and_3_out, and_4_out, and_5_out, and_6_out, and_7_out, and_8_out);
  or or_3 (D1, and_9_out, and_10_out, and_11_out, and_12_out, and_13_out, and_14_out);
  or or_4 (D0, and_15_out, and_16_out, and_17_out, and_18_out, and_19_out);

  // Notes on the sheet:
  //   FUNCIONAMENTO TA VERIFICADO
  //   SE TIVER PROBLEMA AQ N Ë
endmodule

module outWrites (
  input  data_av,
  input  Q3,
  input  Q2,
  input  Q1,
  input  Q0,
  output WrState,
  output WrStateSize,
  output WrTextSize,
  output WrKeyStream,
  output WrDataIn,
  output Wr_J,
  output Wr_I,
  output Wr_K,
  output WrTemp
);

  wire and_2_out, and_3_out, and_9_out, and_10_out, and_11_out, and_12_out, not_1_out, not_2_out, not_3_out,
       not_4_out, not_5_out, not_6_out, not_7_out, not_8_out, not_9_out, not_10_out, not_11_out, not_12_out,
       not_13_out, not_14_out, not_15_out, not_16_out, not_17_out, not_18_out, not_19_out, not_20_out,
       not_21_out, not_22_out, not_23_out, not_24_out, not_25_out, not_26_out, not_27_out, not_28_out;

  not not_1 (not_1_out, Q3);
  not not_2 (not_2_out, Q2);
  not not_3 (not_3_out, Q1);
  not not_4 (not_4_out, Q0);
  not not_5 (not_5_out, Q3);
  not not_6 (not_6_out, Q2);
  not not_7 (not_7_out, Q1);
  not not_8 (not_8_out, Q2);
  not not_9 (not_9_out, Q1);
  not not_10 (not_10_out, Q0);
  not not_11 (not_11_out, Q3);
  not not_12 (not_12_out, Q2);
  not not_13 (not_13_out, Q0);
  not not_14 (not_14_out, Q3);
  not not_15 (not_15_out, Q2);
  not not_16 (not_16_out, Q3);
  not not_17 (not_17_out, Q0);
  not not_18 (not_18_out, Q3);
  not not_19 (not_19_out, Q3);
  not not_20 (not_20_out, Q1);
  not not_21 (not_21_out, Q1);
  not not_22 (not_22_out, Q0);
  not not_23 (not_23_out, Q3);
  not not_24 (not_24_out, Q2);
  not not_25 (not_25_out, Q2);
  not not_26 (not_26_out, Q1);
  not not_27 (not_27_out, Q0);
  not not_28 (not_28_out, Q2);
  and and_1 (WrState, data_av, not_1_out, not_2_out, not_3_out, not_4_out);
  and and_2 (and_2_out, data_av, not_5_out, not_6_out, not_7_out, Q0);
  and and_3 (and_3_out, data_av, Q3, not_8_out, not_9_out, not_10_out);
  and and_4 (WrTextSize, data_av, not_11_out, not_12_out, Q1, not_13_out);
  and and_5 (WrKeyStream, data_av, not_14_out, not_15_out, Q1, Q0);
  and and_6 (WrDataIn, not_16_out, Q2, Q1, not_17_out);
  and and_7 (Wr_J, not_18_out, Q2, Q1, Q0);
  and and_8 (Wr_I, not_19_out, Q2, not_20_out, Q0);
  and and_9 (and_9_out, Q3, Q2, not_21_out, not_22_out);
  and and_10 (and_10_out, data_av, not_23_out, not_24_out, Q1, Q0);
  and and_11 (and_11_out, Q3, not_25_out, not_26_out, not_27_out);
  and and_12 (and_12_out, Q3, not_28_out, Q1, Q0);
  or or_1 (WrStateSize, and_2_out, and_3_out);
  or or_2 (Wr_K, and_9_out, and_10_out);
  or or_3 (WrTemp, and_11_out, and_12_out);
endmodule

module outMux (
  input  Q3,
  input  Q2,
  input  Q1,
  input  Q0,
  output MOUT,
  output MADRK,
  output [1:0] MS2,
  output [1:0] MS1,
  output MS0,
  output MCOMP
);

  wire and_1_out, and_2_out, and_5_out, and_6_out, and_7_out, and_8_out, and_9_out, and_10_out, and_11_out,
       and_12_out, and_13_out, not_1_out, not_2_out, not_3_out, not_4_out, not_5_out, not_6_out, not_7_out,
       not_8_out, not_9_out, not_10_out, not_11_out, not_12_out, not_13_out, not_14_out, not_15_out,
       not_16_out, not_17_out, not_18_out, not_19_out;

  not not_1 (not_1_out, Q2);
  not not_2 (not_2_out, Q1);
  and and_1 (and_1_out, not_1_out, not_2_out, Q0);
  and and_2 (and_2_out, Q3, Q2);
  and and_3 (MADRK, Q3, Q2);
  not not_3 (not_3_out, Q2);
  not not_4 (not_4_out, Q0);
  not not_5 (not_5_out, Q1);
  not not_6 (not_6_out, Q0);
  not not_7 (not_7_out, Q3);
  not not_8 (not_8_out, Q2);
  not not_9 (not_9_out, Q0);
  not not_10 (not_10_out, Q2);
  and and_4 (MS1[1], Q3, not_10_out, not_11_out);
  not not_11 (not_11_out, Q1);
  not not_12 (not_12_out, Q3);
  and and_5 (and_5_out, not_12_out, Q2, Q0);
  not not_13 (not_13_out, Q2);
  and and_6 (and_6_out, Q3, not_13_out, not_14_out);
  not not_14 (not_14_out, Q0);
  not not_15 (not_15_out, Q3);
  and and_7 (and_7_out, not_15_out, Q2, Q0);
  not not_16 (not_16_out, Q2);
  and and_8 (and_8_out, Q3, not_16_out, not_17_out);
  not not_17 (not_17_out, Q1);
  not not_18 (not_18_out, Q2);
  and and_9 (and_9_out, Q3, not_18_out, not_19_out);
  not not_19 (not_19_out, Q0);
  or or_1 (MOUT, and_1_out, and_2_out);
  and and_10 (and_10_out, Q3, not_3_out, Q1, not_4_out);
  or or_2 (MS2[1], and_10_out, and_11_out);
  and and_11 (and_11_out, Q3, Q2, not_5_out, not_6_out);
  and and_12 (and_12_out, not_7_out, Q2, Q1, Q0);
  or or_3 (MS2[0], and_12_out, and_13_out);
  and and_13 (and_13_out, Q3, not_8_out, Q1, not_9_out);
  or or_4 (MS1[0], and_5_out, and_6_out);
  or or_5 (MS0, and_7_out, and_8_out, and_9_out);
  and and_14 (MCOMP, ~Q3, Q2, ~Q1, ~Q0);  // AND_Gate
endmodule

module outGeral (
  input  status,
  input  Q3,
  input  Q2,
  input  Q1,
  input  Q0,
  input  data_av,
  output Id,
  output Sel,
  output Done,
  output Rst
);

  wire and_1_out, and_2_out, and_3_out, and_4_out, and_5_out, not_1_out, not_2_out, not_3_out, not_4_out,
       not_5_out, not_6_out, not_7_out;

  not not_1 (not_1_out, Q0);
  not not_2 (not_2_out, Q1);
  not not_3 (not_3_out, Q0);
  not not_4 (not_4_out, status);
  not not_5 (not_5_out, Q3);
  not not_6 (not_6_out, Q1);
  not not_7 (not_7_out, Q0);
  and and_1 (and_1_out, Q2, Q0);
  and and_2 (and_2_out, Q3, Q1, not_1_out);
  and and_3 (and_3_out, Q2, Q0);
  and and_4 (and_4_out, Q3, not_2_out);
  and and_5 (and_5_out, Q3, not_3_out);
  and and_6 (Done, not_4_out, not_5_out, Q2, not_6_out, not_7_out);
  and and_7 (Rst, ~data_av, ~Q3, ~Q2, ~Q1, ~Q0);  // AND_Gate
  or or_1 (Id, and_1_out, and_2_out);
  or or_2 (Sel, and_3_out, and_4_out, and_5_out);
endmodule

module sincronizador (
  input  in,
  input  clk,
  output bt_out
);

  wire and_1_out, and_2_out, FF0_q, FF1_q, not_1_out, not_2_out, not_3_out, or_1_out, reset_out;

  Button reset (.out(reset_out));
  or or_1 (or_1_out, FF1_q, FF0_q);
  not not_1 (not_1_out, FF1_q);
  not not_2 (not_2_out, FF0_q);
  and and_1 (and_1_out, or_1_out, in);
  and and_2 (and_2_out, not_1_out, not_2_out, in);
  D_Flip_Flop FF1 (.clk(clk), .D(and_1_out), .Q(FF1_q), .reset(reset_out));  // open: Qn, preset, en
  D_Flip_Flop FF0 (.clk(clk), .D(and_2_out), .Q(FF0_q), .reset(reset_out));  // open: Qn, preset, en
  not not_3 (not_3_out, FF1_q);
  and and_3 (bt_out, not_3_out, FF0_q);
endmodule
